# Fritzing sketch sketch_v1 (saved by Fritzing 0.9.3b)
breadboards: 1

parts:
  U1 = TA7291P [package=HSIP10-P-2.54(THT)]
  Mod1 = Microbit
  VCC1 = Battery
  M1 = DC Motor
  C1 = Ceramic Capacitor [capacitance=100nF package="100 mil [THT, multilayer]"]  # not connected
  SPKR1 = Loudspeaker

nets:
  GND: U1.GND, Mod1.GND, VCC1.-, SPKR1.pin1
  N1: U1.OUT1, M1.pin_2
  N2: U1.Vref, Mod1.P0, SPKR1.pin2
  N3: U1.IN1, Mod1.P1
  N4: U1.IN2, Mod1.P2
  VCC: U1.Vcc, Mod1.3V3
  N5: U1.Vs, VCC1.+
  N6: U1.OUT2, M1.pin_1

custom parts:
  TA7291P: The IC are Full-Bridge Driver. 4 modes available (CW / CCW / STOP / BRAKE) and PWM control. Output current:1.0 A (AVE.) 2.0 A (PEAK)
  Microbit: BBC Microbit Fritzing part. May 2019 expanded to include schematic and pcb views as well as breadboard. PCB view assumes an Adafruit PRODUCT ID: 3342 2x40 Right Angle through hole edge connector (although others will probably work as well). The pcb svg is custom (see forum article http://forum.fritzing.org/t/making-edge-connectors-and-both-side-smd-parts/7287 for an explaination if you need to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
